// Logisim project 4BIT_COMPUTING_DEVICE.circ as structural Verilog: 1 circuit, main circuit main
module main (
  input  [3:0] in_1,
  input  [3:0] in_2,
  input  [3:0] in_3,
  output [3:0] out_4
);

  wire main_1_out_14, main_2_out_11, main_2_out_12, main_2_out_13, main_2_out_14, main_3_p5, main_3_p6,
       main_3_p11, main_3_p12, main_4_out_11, main_4_out_12, main_4_out_13, main_4_out_14, main_5_out_11,
       main_5_out_12, main_5_out_13, main_5_out_14, main_6_out_11, main_6_out_12, main_6_out_13,
       main_6_out_14, main_7_out_11, main_7_out_12, main_7_out_13, main_7_out_14, main_8_out_11,
       main_8_out_12, main_8_out_13, main_8_out_14, main_9_out_11, main_9_out_12, main_9_out_13,
       main_9_out_14, main_10_out_11, main_10_out_12, main_10_out_13, main_10_out_14, main_11_out_11,
       main_11_out_12, main_11_out_13, main_11_out_14, main_12_out_11, main_12_out_12, main_12_out_13,
       main_12_out_14, main_13_out_11, main_13_out_12, main_13_out_13, main_13_out_14, main_15_out_11,
       main_15_out_12, main_15_out_13, main_15_out_14, main_16_out_11, main_16_out_12, main_16_out_13,
       main_16_out_14, main_17_out_11, main_17_out_12, main_17_out_13, main_17_out_14, main_18_out_11,
       main_18_out_12, main_18_out_13, main_18_out_14, main_19_out_11, main_19_out_12, main_19_out_13,
       main_19_out_14, main_20_out_11, main_20_out_12, main_20_out_13, main_20_out_14, main_21_out_11,
       main_21_out_12, main_21_out_13, main_21_out_14, main_22_out_11, main_22_out_12, main_22_out_13,
       main_22_out_14, undriven, undriven_2, undriven_3, undriven_4, undriven_5, undriven_6, undriven_7,
       undriven_8, undriven_9;
  wire [3:0] main_23_out_2, main_27_out_2;

  _7404_NOT_main main_1 (
    .in_7(main_2_out_11), .out_14(main_1_out_14));  // open: in_2, in_3, out_9, in_4, out_10, in_8, in_1, in_5, in_6, out_12, out_13, out_11
  _7408_AND_main main_2 (
    .in_2(in_3[0]), .in_3(main_2_out_12), .out_11(main_2_out_11), .in_4(in_3[1]), .in_5(main_2_out_14),
    .out_12(main_2_out_12), .in_6(1'b1), .in_7(in_3[3]), .out_13(main_2_out_13), .in_8(main_2_out_13),
    .in_9(in_3[2]), .out_14(main_2_out_14));  // open: GND, Vcc
  // _7408_AND_main main_3: pin names not known; wires that end beside it: main_2_out_11, main_2_out_11, in_1[3], in_1[0], main_3_p5, main_3_p6, main_2_out_11, main_2_out_11, in_1[2], in_1[1], main_3_p11, main_3_p12
  _7432_OR_main main_4 (
    .in_2(in_3[0]), .in_3(in_2[0]), .out_11(main_4_out_11), .in_4(in_3[1]), .in_5(in_2[1]),
    .out_12(main_4_out_12), .in_6(in_3[3]), .in_7(in_2[3]), .out_13(main_4_out_13), .in_8(in_3[2]),
    .in_9(in_2[2]), .out_14(main_4_out_14));  // open: GND, Vcc
  _7432_OR_main main_5 (
    .in_2(in_1[0]), .in_3(in_3[0]), .out_11(main_5_out_11), .in_4(in_1[1]), .in_5(in_3[1]),
    .out_12(main_5_out_12), .in_6(in_1[3]), .in_7(in_3[3]), .out_13(main_5_out_13), .in_8(in_1[2]),
    .in_9(in_3[2]), .out_14(main_5_out_14));  // open: GND, Vcc
  _7432_OR_main main_6 (
    .in_2(in_1[0]), .in_3(in_2[0]), .out_11(main_6_out_11), .in_4(in_1[1]), .in_5(in_2[1]),
    .out_12(main_6_out_12), .in_6(in_1[3]), .in_7(in_2[3]), .out_13(main_6_out_13), .in_8(in_1[2]),
    .in_9(in_2[2]), .out_14(main_6_out_14));  // open: GND, Vcc
  _7432_OR_main main_7 (
    .in_2(in_1[0]), .in_3(in_2[0]), .out_11(main_7_out_11), .in_4(in_1[1]), .in_5(in_2[1]),
    .out_12(main_7_out_12), .in_6(in_1[3]), .in_7(in_2[3]), .out_13(main_7_out_13), .in_8(in_1[2]),
    .in_9(in_2[2]), .out_14(main_7_out_14));  // open: GND, Vcc
  _7486_XOR_main main_8 (
    .in_2(in_1[0]), .in_3(in_2[0]), .out_11(main_8_out_11), .in_4(in_1[1]), .in_5(in_2[1]),
    .out_12(main_8_out_12), .in_6(in_1[3]), .in_7(in_2[3]), .out_13(main_8_out_13), .in_8(in_1[2]),
    .in_9(in_2[2]), .out_14(main_8_out_14));  // open: GND, Vcc
  _7402_NOR_main main_9 (
    .in_3(in_1[0]), .in_2(in_2[0]), .out_11(main_9_out_11), .in_5(in_2[1]), .in_4(in_1[1]),
    .out_12(main_9_out_12), .in_7(in_1[3]), .in_6(in_2[3]), .out_13(main_9_out_13), .GND(in_1[2]),
    .in_8(in_2[2]), .out_14(main_9_out_14));  // open: in_10, Vcc
  _7432_OR_main main_10 (
    .in_2(in_1[0]), .in_3(in_2[0]), .out_11(main_10_out_11), .in_4(in_1[1]), .in_5(in_2[1]),
    .out_12(main_10_out_12), .in_6(in_1[3]), .in_7(in_2[3]), .out_13(main_10_out_13), .in_8(in_1[2]),
    .in_9(in_2[2]), .out_14(main_10_out_14));  // open: GND, Vcc
  _7408_AND_main main_11 (
    .in_2(in_1[0]), .in_3(in_2[0]), .out_11(main_11_out_11), .in_4(in_1[1]), .in_5(in_2[1]),
    .out_12(main_11_out_12), .in_6(in_1[3]), .in_7(in_2[3]), .out_13(main_11_out_13), .in_8(in_1[2]),
    .in_9(in_2[2]), .out_14(main_11_out_14));  // open: GND, Vcc
  _7408_AND_main main_12 (
    .in_2(main_1_out_14), .in_3(in_2[0]), .out_11(main_12_out_11), .in_4(main_1_out_14), .in_5(in_2[1]),
    .out_12(main_12_out_12), .in_6(main_1_out_14), .in_7(in_2[3]), .out_13(main_12_out_13),
    .in_8(main_1_out_14), .in_9(in_2[2]), .out_14(main_12_out_14));  // open: GND, Vcc
  _7432_OR_main main_13 (
    .in_2(main_3_p6), .in_3(main_12_out_11), .out_11(main_13_out_11), .in_4(main_12_out_12),
    .in_5(main_3_p12), .out_12(main_13_out_12), .in_6(main_3_p5), .in_7(main_12_out_13),
    .out_13(main_13_out_13), .in_8(main_3_p11), .in_9(main_12_out_14), .out_14(main_13_out_14));  // open: GND, Vcc
  _7408_AND_main main_14 (
    .in_2(main_13_out_11), .in_3(undriven), .in_4(main_13_out_12), .in_5(undriven), .in_6(undriven),
    .in_7(main_13_out_13), .in_8(undriven), .in_9(main_13_out_14));  // open: out_11, out_12, GND, Vcc, out_13, out_14
  _7408_AND_main main_15 (
    .in_2(main_4_out_11), .in_3(undriven_6), .out_11(main_15_out_11), .in_4(main_4_out_12),
    .in_5(undriven_6), .out_12(main_15_out_12), .in_6(main_4_out_13), .in_7(undriven_6),
    .out_13(main_15_out_13), .in_8(main_4_out_14), .in_9(undriven_6), .out_14(main_15_out_14));  // open: GND, Vcc
  _7408_AND_main main_16 (
    .in_2(main_5_out_11), .in_3(undriven_7), .out_11(main_16_out_11), .in_4(main_5_out_12),
    .in_5(undriven_7), .out_12(main_16_out_12), .in_6(main_5_out_13), .in_7(undriven_7),
    .out_13(main_16_out_13), .in_8(main_5_out_14), .in_9(undriven_7), .out_14(main_16_out_14));  // open: GND, Vcc
  _7408_AND_main main_17 (
    .in_2(main_6_out_11), .in_3(undriven_8), .out_11(main_17_out_11), .in_4(main_6_out_12),
    .in_5(undriven_8), .out_12(main_17_out_12), .in_6(main_6_out_13), .in_7(undriven_8),
    .out_13(main_17_out_13), .in_8(main_6_out_14), .in_9(undriven_8), .out_14(main_17_out_14));  // open: GND, Vcc
  _7408_AND_main main_18 (
    .in_2(main_7_out_11), .in_3(undriven_9), .out_11(main_18_out_11), .in_4(main_7_out_12),
    .in_5(undriven_9), .out_12(main_18_out_12), .in_6(main_7_out_13), .in_7(undriven_9),
    .out_13(main_18_out_13), .in_8(main_7_out_14), .in_9(undriven_9), .out_14(main_18_out_14));  // open: GND, Vcc
  _7408_AND_main main_19 (
    .in_2(main_8_out_11), .in_3(undriven_2), .out_11(main_19_out_11), .in_4(main_8_out_12),
    .in_5(undriven_2), .out_12(main_19_out_12), .in_6(main_8_out_13), .in_7(undriven_2),
    .out_13(main_19_out_13), .in_8(main_8_out_14), .in_9(undriven_2), .out_14(main_19_out_14));  // open: GND, Vcc
  _7408_AND_main main_20 (
    .in_2(main_9_out_11), .in_3(undriven_3), .out_11(main_20_out_11), .in_4(main_9_out_12),
    .in_5(undriven_3), .out_12(main_20_out_12), .in_6(main_9_out_13), .in_7(undriven_3),
    .out_13(main_20_out_13), .in_8(main_9_out_14), .in_9(undriven_3), .out_14(main_20_out_14));  // open: GND, Vcc
  _7408_AND_main main_21 (
    .in_2(main_10_out_11), .in_3(undriven_4), .out_11(main_21_out_11), .in_4(main_10_out_12),
    .in_5(undriven_4), .out_12(main_21_out_12), .in_6(main_10_out_13), .in_7(undriven_4),
    .out_13(main_21_out_13), .in_8(main_10_out_14), .in_9(undriven_4), .out_14(main_21_out_14));  // open: GND, Vcc
  _7408_AND_main main_22 (
    .in_2(main_11_out_11), .in_3(undriven_5), .out_11(main_22_out_11), .in_4(main_11_out_12),
    .in_5(undriven_5), .out_12(main_22_out_12), .in_6(main_11_out_13), .in_7(undriven_5),
    .out_13(main_22_out_13), .in_8(main_11_out_14), .in_9(undriven_5), .out_14(main_22_out_14));  // open: GND, Vcc
  DIODE_main main_23 (.in_1(main_15_out_11), .out_2(main_23_out_2[0]));
  DIODE_main main_24 (.in_1(main_15_out_12), .out_2(main_23_out_2[1]));
  DIODE_main main_25 (.in_1(main_15_out_14), .out_2(main_23_out_2[2]));
  DIODE_main main_26 (.in_1(main_15_out_13), .out_2(main_23_out_2[3]));
  DIODE_main main_27 (.in_1(main_16_out_11), .out_2(main_27_out_2[0]));
  DIODE_main main_28 (.in_1(main_16_out_12), .out_2(main_27_out_2[1]));
  DIODE_main main_29 (.in_1(main_16_out_14), .out_2(main_27_out_2[2]));
  DIODE_main main_30 (.in_1(main_16_out_13), .out_2(main_27_out_2[3]));
  DIODE_main main_31 (.in_1(main_17_out_11));  // open: out_2
  DIODE_main main_32 (.in_1(main_17_out_12), .out_2(out_4[0]));
  DIODE_main main_33 (.in_1(main_17_out_14), .out_2(out_4[1]));
  DIODE_main main_34 (.in_1(main_17_out_13), .out_2(out_4[2]));
  DIODE_main main_35 (.in_1(main_18_out_11), .out_2(out_4[1]));
  DIODE_main main_36 (.in_1(main_18_out_12), .out_2(out_4[2]));
  DIODE_main main_37 (.in_1(main_18_out_14), .out_2(out_4[3]));
  DIODE_main main_38 (.in_1(main_18_out_13));  // open: out_2
  DIODE_main main_39 (.in_1(main_19_out_11), .out_2(out_4[0]));
  DIODE_main main_40 (.in_1(main_19_out_12), .out_2(out_4[1]));
  DIODE_main main_41 (.in_1(main_19_out_14), .out_2(out_4[2]));
  DIODE_main main_42 (.in_1(main_19_out_13), .out_2(out_4[3]));
  DIODE_main main_43 (.in_1(main_20_out_11), .out_2(out_4[0]));
  DIODE_main main_44 (.in_1(main_20_out_12), .out_2(out_4[1]));
  DIODE_main main_45 (.in_1(main_20_out_14), .out_2(out_4[2]));
  DIODE_main main_46 (.in_1(main_20_out_13), .out_2(out_4[3]));
  DIODE_main main_47 (.in_1(main_21_out_11), .out_2(out_4[0]));
  DIODE_main main_48 (.in_1(main_21_out_12), .out_2(out_4[1]));
  DIODE_main main_49 (.in_1(main_21_out_14), .out_2(out_4[2]));
  DIODE_main main_50 (.in_1(main_21_out_13), .out_2(out_4[3]));
  DIODE_main main_51 (.in_1(main_22_out_11), .out_2(out_4[0]));
  DIODE_main main_52 (.in_1(main_22_out_12), .out_2(out_4[1]));
  DIODE_main main_53 (.in_1(main_22_out_14), .out_2(out_4[2]));
  DIODE_main main_54 (.in_1(main_22_out_13), .out_2(out_4[3]));
endmodule
